// Logisim project HexMuxer.circ as structural Verilog: 1 circuit, main circuit main
module main (
);

  wire and_1_out, and_2_out, and_3_out, and_4_out, and_5_out, and_6_out, and_7_out, and_8_out, and_9_out,
       and_10_out, and_11_out, and_12_out, and_13_out, and_14_out, and_15_out, and_16_out, and_17_out,
       and_18_out, and_19_out, and_20_out, and_21_out, and_22_out, and_23_out, and_24_out, clock_1_out,
       decoder_1_out0, decoder_1_out1, decoder_1_out2, decoder_1_out3, decoder_1_out4, decoder_1_out5,
       decoder_1_out6;
  wire [2:0] counter_1_q;
  wire [3:0] or_1_out;

  Decoder #(.select(3)) decoder_1 (
    .out0(decoder_1_out0), .out1(decoder_1_out1), .out2(decoder_1_out2), .out3(decoder_1_out3),
    .out4(decoder_1_out4), .out5(decoder_1_out5), .out6(decoder_1_out6), .sel(counter_1_q));  // open: out7, en
  Counter #(.width(3), .max('h7)) counter_1 (
    .Q(counter_1_q), .clk(clock_1_out), .clr(decoder_1_out6));  // open: load, D, count, carry
  Clock clock_1 (.out(clock_1_out));
  Hex_Digit_Display hex_digit_display_1 (.value(or_1_out));  // open: dp
  and and_1 (and_1_out, decoder_1_out0, 1'b0);
  and and_2 (and_2_out, decoder_1_out1, 1'b1);
  and and_3 (and_3_out, decoder_1_out3, 1'b0);
  and and_4 (and_4_out, decoder_1_out2, 1'b0);
  or or_1 (or_1_out[0], and_1_out, and_2_out, and_4_out, and_3_out, and_6_out, and_5_out);
  LED led_1 (.in(or_1_out[0]));
  and and_5 (and_5_out, decoder_1_out5, 1'b1);
  and and_6 (and_6_out, decoder_1_out4, 1'b0);
  and and_7 (and_7_out, decoder_1_out0, 1'b0);
  and and_8 (and_8_out, decoder_1_out2, 1'b1);
  and and_9 (and_9_out, decoder_1_out1, 1'b0);
  or or_2 (or_1_out[1], and_7_out, and_9_out, and_8_out, and_11_out, and_10_out, and_14_out);
  LED led_2 (.in(or_1_out[1]));
  and and_10 (and_10_out, decoder_1_out4, 1'b0);
  and and_11 (and_11_out, decoder_1_out3, 1'b0);
  and and_12 (and_12_out, decoder_1_out0, 1'b0);
  and and_13 (and_13_out, decoder_1_out1, 1'b0);
  and and_14 (and_14_out, decoder_1_out5, 1'b1);
  or or_3 (or_1_out[2], and_12_out, and_13_out, and_16_out, and_15_out, and_18_out, and_19_out);
  and and_15 (and_15_out, decoder_1_out3, 1'b1);
  and and_16 (and_16_out, decoder_1_out2, 1'b0);
  LED led_3 (.in(or_1_out[2]));
  and and_17 (and_17_out, decoder_1_out0, 1'b0);
  and and_18 (and_18_out, decoder_1_out4, 1'b0);
  and and_19 (and_19_out, decoder_1_out5, 1'b1);
  and and_20 (and_20_out, decoder_1_out2, 1'b0);
  and and_21 (and_21_out, decoder_1_out1, 1'b0);
  or or_4 (or_1_out[3], and_17_out, and_21_out, and_20_out, and_22_out, and_24_out, and_23_out);
  LED led_4 (.in(or_1_out[3]));
  and and_22 (and_22_out, decoder_1_out3, 1'b0);
  and and_23 (and_23_out, decoder_1_out5, 1'b1);
  and and_24 (and_24_out, decoder_1_out4, 1'b1);
  LED led_5 (.in(decoder_1_out0));
  LED led_6 (.in(decoder_1_out1));
  LED led_7 (.in(decoder_1_out2));
  LED led_8 (.in(decoder_1_out3));
  LED led_9 (.in(decoder_1_out4));
  LED led_10 (.in(decoder_1_out5));
endmodule
