// Logisim project sevensegment-hex-decoder.circ as structural Verilog: 1 circuit, main circuit main
module main (
  output i1,
  output i2,
  output i3,
  output i4,
  output i5,
  output i6,
  output i7,
  output i8,
  output i9,
  output i10,
  output i11,
  output i12,
  output i13,
  output i14
);

  wire A_out, B_out, buffer_43_out, buffer_51_out, buffer_57_out, buffer_64_out, buffer_72_out,
       buffer_79_out, buffer_87_out, C_out, clock_1_out, D_out, E_out, F_out, G_out, not_1_out, not_2_out,
       not_3_out, not_4_out, pull_resistor_1_node, pull_resistor_2_node, pull_resistor_3_node,
       pull_resistor_4_node, pull_resistor_5_node, pull_resistor_6_node, pull_resistor_7_node,
       pull_resistor_8_node, pull_resistor_9_node, pull_resistor_10_node, pull_resistor_11_node,
       pull_resistor_12_node, pull_resistor_13_node, pull_resistor_14_node;
  wire [3:0] counter_1_q;

  not not_1 (not_1_out, counter_1_q[3]);
  not not_2 (not_2_out, counter_1_q[2]);
  not not_3 (not_3_out, counter_1_q[1]);
  not not_4 (not_4_out, counter_1_q[0]);
  Hex_Digit_Display hex_digit_display_1 (.value(counter_1_q));  // open: dp
  Counter #(.width(4), .max('hf)) counter_1 (.Q(counter_1_q), .clk(clock_1_out));  // open: load, D, count, carry, clr
  Clock clock_1 (.out(clock_1_out));
  Pull_Resistor #(.pull(1)) pull_resistor_1 (.node(pull_resistor_1_node));
  Pull_Resistor #(.pull(1)) pull_resistor_2 (.node(pull_resistor_2_node));
  buf buffer_1 (pull_resistor_1_node, counter_1_q[1]);
  buf buffer_2 (pull_resistor_1_node, counter_1_q[0]);
  buf buffer_3 (pull_resistor_1_node, not_1_out);
  buf buffer_4 (pull_resistor_2_node, not_4_out);
  buf buffer_5 (pull_resistor_2_node, not_3_out);
  buf buffer_6 (pull_resistor_2_node, not_1_out);
  and u_i1 (i1, not_4_out, not_3_out, not_1_out);
  and u_i2 (i2, counter_1_q[0], counter_1_q[1], not_1_out);
  Pull_Resistor #(.pull(1)) pull_resistor_3 (.node(pull_resistor_3_node));
  Pull_Resistor #(.pull(1)) pull_resistor_4 (.node(pull_resistor_4_node));
  Pull_Resistor #(.pull(1)) pull_resistor_5 (.node(pull_resistor_5_node));
  buf buffer_7 (pull_resistor_4_node, not_2_out);
  buf buffer_8 (pull_resistor_4_node, counter_1_q[1]);
  buf buffer_9 (pull_resistor_4_node, not_1_out);
  buf buffer_10 (pull_resistor_3_node, not_2_out);
  buf buffer_11 (pull_resistor_5_node, not_4_out);
  buf buffer_12 (pull_resistor_3_node, not_3_out);
  buf buffer_13 (pull_resistor_5_node, counter_1_q[1]);
  and u_i3 (i3, not_3_out, not_2_out);
  and u_i5 (i5, not_4_out, counter_1_q[1], not_1_out);
  and u_i4 (i4, counter_1_q[1], not_2_out, not_1_out);
  Pull_Resistor #(.pull(1)) pull_resistor_6 (.node(pull_resistor_6_node));
  Pull_Resistor #(.pull(1)) pull_resistor_7 (.node(pull_resistor_7_node));
  buf buffer_14 (pull_resistor_6_node, counter_1_q[2]);
  buf buffer_15 (pull_resistor_6_node, not_1_out);
  buf buffer_16 (pull_resistor_6_node, not_4_out);
  buf buffer_17 (pull_resistor_7_node, counter_1_q[2]);
  buf buffer_18 (pull_resistor_7_node, counter_1_q[0]);
  buf buffer_19 (pull_resistor_5_node, not_1_out);
  buf buffer_20 (pull_resistor_7_node, not_3_out);
  and u_i7 (i7, counter_1_q[0], not_3_out, counter_1_q[2], counter_1_q[3]);
  and u_i6 (i6, not_4_out, counter_1_q[2], not_1_out);
  Pull_Resistor #(.pull(1)) pull_resistor_8 (.node(pull_resistor_8_node));
  Pull_Resistor #(.pull(1)) pull_resistor_9 (.node(pull_resistor_9_node));
  buf buffer_21 (pull_resistor_9_node, not_2_out);
  buf buffer_22 (pull_resistor_9_node, counter_1_q[0]);
  buf buffer_23 (pull_resistor_9_node, counter_1_q[3]);
  buf buffer_24 (pull_resistor_9_node, counter_1_q[1]);
  buf buffer_25 (pull_resistor_8_node, counter_1_q[0]);
  buf buffer_26 (pull_resistor_7_node, counter_1_q[3]);
  buf buffer_27 (pull_resistor_8_node, not_3_out);
  and u_i8 (i8, counter_1_q[0], counter_1_q[1], not_2_out, counter_1_q[3]);
  Pull_Resistor #(.pull(1)) pull_resistor_10 (.node(pull_resistor_10_node));
  Pull_Resistor #(.pull(1)) pull_resistor_11 (.node(pull_resistor_11_node));
  buf buffer_28 (pull_resistor_10_node, counter_1_q[3]);
  buf buffer_29 (pull_resistor_10_node, counter_1_q[1]);
  buf buffer_30 (pull_resistor_10_node, counter_1_q[2]);
  buf buffer_31 (pull_resistor_8_node, counter_1_q[2]);
  buf buffer_32 (pull_resistor_11_node, not_3_out);
  buf buffer_33 (pull_resistor_8_node, not_1_out);
  buf buffer_34 (pull_resistor_11_node, not_4_out);
  and u_i9 (i9, counter_1_q[0], not_3_out, counter_1_q[2], not_1_out);
  and u_i11 (i11, not_4_out, not_3_out, not_2_out);
  and u_i10 (i10, counter_1_q[1], counter_1_q[2], counter_1_q[3]);
  Pull_Resistor #(.pull(1)) pull_resistor_12 (.node(pull_resistor_12_node));
  Pull_Resistor #(.pull(1)) pull_resistor_13 (.node(pull_resistor_13_node));
  Pull_Resistor #(.pull(1)) pull_resistor_14 (.node(pull_resistor_14_node));
  buf buffer_35 (pull_resistor_12_node, not_4_out);
  buf buffer_36 (pull_resistor_12_node, counter_1_q[2]);
  buf buffer_37 (pull_resistor_12_node, counter_1_q[3]);
  buf buffer_38 (pull_resistor_13_node, not_4_out);
  buf buffer_39 (pull_resistor_14_node, not_2_out);
  buf buffer_40 (pull_resistor_14_node, counter_1_q[3]);
  buf buffer_41 (pull_resistor_14_node, not_3_out);
  buf buffer_42 (pull_resistor_11_node, not_2_out);
  and u_i13 (i13, not_3_out, not_2_out, counter_1_q[3]);
  and u_i12 (i12, not_4_out, counter_1_q[2], counter_1_q[3]);
  buf buffer_43 (buffer_43_out, pull_resistor_1_node);
  buf buffer_44 (buffer_43_out, pull_resistor_5_node);
  buf buffer_45 (buffer_43_out, pull_resistor_8_node);
  buf buffer_46 (buffer_43_out, pull_resistor_10_node);
  buf buffer_47 (buffer_43_out, pull_resistor_11_node);
  buf buffer_48 (buffer_43_out, pull_resistor_12_node);
  buf buffer_49 (buffer_43_out, pull_resistor_14_node);
  buf buffer_50 (buffer_43_out, pull_resistor_13_node);
  buf buffer_51 (buffer_51_out, pull_resistor_2_node);
  buf buffer_52 (buffer_51_out, pull_resistor_1_node);
  buf buffer_53 (buffer_51_out, pull_resistor_3_node);
  buf buffer_54 (buffer_51_out, pull_resistor_4_node);
  buf buffer_55 (buffer_51_out, pull_resistor_7_node);
  buf buffer_56 (buffer_51_out, pull_resistor_13_node);
  buf buffer_57 (buffer_57_out, pull_resistor_1_node);
  buf buffer_58 (buffer_57_out, pull_resistor_3_node);
  buf buffer_59 (buffer_57_out, pull_resistor_6_node);
  buf buffer_60 (buffer_57_out, pull_resistor_7_node);
  buf buffer_61 (buffer_57_out, pull_resistor_9_node);
  buf buffer_62 (buffer_57_out, pull_resistor_8_node);
  buf buffer_63 (buffer_57_out, pull_resistor_13_node);
  buf buffer_64 (buffer_64_out, pull_resistor_4_node);
  buf buffer_65 (buffer_64_out, pull_resistor_5_node);
  buf buffer_66 (buffer_64_out, pull_resistor_7_node);
  buf buffer_67 (buffer_64_out, pull_resistor_9_node);
  buf buffer_68 (buffer_64_out, pull_resistor_8_node);
  buf buffer_69 (buffer_64_out, pull_resistor_11_node);
  buf buffer_70 (buffer_64_out, pull_resistor_12_node);
  buf buffer_71 (buffer_64_out, pull_resistor_14_node);
  buf buffer_72 (buffer_72_out, pull_resistor_5_node);
  buf buffer_73 (buffer_72_out, pull_resistor_7_node);
  buf buffer_74 (buffer_72_out, pull_resistor_9_node);
  buf buffer_75 (buffer_72_out, pull_resistor_10_node);
  buf buffer_76 (buffer_72_out, pull_resistor_11_node);
  buf buffer_77 (buffer_72_out, pull_resistor_12_node);
  buf buffer_78 (buffer_72_out, pull_resistor_13_node);
  buf buffer_79 (buffer_79_out, pull_resistor_6_node);
  buf buffer_80 (buffer_79_out, pull_resistor_9_node);
  buf buffer_81 (buffer_79_out, pull_resistor_8_node);
  buf buffer_82 (buffer_79_out, pull_resistor_10_node);
  buf buffer_83 (buffer_79_out, pull_resistor_11_node);
  buf buffer_84 (buffer_79_out, pull_resistor_12_node);
  buf buffer_85 (buffer_79_out, pull_resistor_14_node);
  buf buffer_86 (buffer_79_out, pull_resistor_13_node);
  buf buffer_87 (buffer_87_out, pull_resistor_4_node);
  buf buffer_88 (buffer_87_out, pull_resistor_6_node);
  buf buffer_89 (buffer_87_out, pull_resistor_7_node);
  buf buffer_90 (buffer_87_out, pull_resistor_9_node);
  buf buffer_91 (buffer_87_out, pull_resistor_8_node);
  buf buffer_92 (buffer_87_out, pull_resistor_10_node);
  buf buffer_93 (buffer_87_out, pull_resistor_14_node);
  buf buffer_94 (buffer_87_out, pull_resistor_13_node);
  buf buffer_95 (pull_resistor_13_node, not_2_out);
  buf buffer_96 (pull_resistor_13_node, counter_1_q[3]);
  _7_Segment_Display u_7_segment_display_1 (
    .g(G_out), .f(F_out), .a(A_out), .b(B_out), .e(E_out), .d(D_out), .c(C_out));  // open: dp
  and u_i14 (i14, not_4_out, not_2_out, counter_1_q[3]);
  Pull_Resistor pull_resistor_15 (.node(buffer_43_out));
  Pull_Resistor pull_resistor_16 (.node(buffer_51_out));
  Pull_Resistor pull_resistor_17 (.node(buffer_57_out));
  Pull_Resistor pull_resistor_18 (.node(buffer_64_out));
  Pull_Resistor pull_resistor_19 (.node(buffer_72_out));
  _7_Segment_Display u_7_segment_display_2 (
    .g(buffer_87_out), .f(buffer_79_out), .a(buffer_43_out), .b(buffer_51_out), .e(buffer_72_out),
    .d(buffer_64_out), .c(buffer_57_out));  // open: dp
  Pull_Resistor pull_resistor_20 (.node(buffer_79_out));
  Pull_Resistor pull_resistor_21 (.node(buffer_87_out));
  or A (A_out, i2, i5, i9, i10, i11, i12, i13, i14);
  or B (B_out, i1, i2, i3, i4, i7, i14);
  or C (C_out, i2, i3, i6, i7, i8, i9, i14);
  or D (D_out, i4, i5, i7, i8, i9, i11, i12, i13);
  or E (E_out, i5, i7, i8, i10, i11, i12, i14);
  or F (F_out, i6, i8, i9, i10, i11, i12, i13, i14);
  or G (G_out, i4, i6, i7, i8, i9, i10, i13, i14);

  // Notes on the sheet:
  //   /0
  //   /1
  //   /2
  //   /3
  //   0
  //   1
  //   2
  //   3
  //   buffer_1 drives only 0 and floats otherwise
  //   buffer_2 drives only 0 and floats otherwise
  //   buffer_3 drives only 0 and floats otherwise
  //   buffer_4 drives only 0 and floats otherwise
  //   buffer_5 drives only 0 and floats otherwise
  //   buffer_6 drives only 0 and floats otherwise
  //   buffer_7 drives only 0 and floats otherwise
  //   buffer_8 drives only 0 and floats otherwise
  //   buffer_9 drives only 0 and floats otherwise
  //   buffer_10 drives only 0 and floats otherwise
  //   buffer_11 drives only 0 and floats otherwise
  //   buffer_12 drives only 0 and floats otherwise
  //   buffer_13 drives only 0 and floats otherwise
  //   buffer_14 drives only 0 and floats otherwise
  //   buffer_15 drives only 0 and floats otherwise
  //   buffer_16 drives only 0 and floats otherwise
  //   buffer_17 drives only 0 and floats otherwise
  //   buffer_18 drives only 0 and floats otherwise
  //   buffer_19 drives only 0 and floats otherwise
  //   buffer_20 drives only 0 and floats otherwise
  //   buffer_21 drives only 0 and floats otherwise
  //   buffer_22 drives only 0 and floats otherwise
  //   buffer_23 drives only 0 and floats otherwise
  //   buffer_24 drives only 0 and floats otherwise
  //   buffer_25 drives only 0 and floats otherwise
  //   buffer_26 drives only 0 and floats otherwise
  //   buffer_27 drives only 0 and floats otherwise
  //   buffer_28 drives only 0 and floats otherwise
  //   buffer_29 drives only 0 and floats otherwise
  //   buffer_30 drives only 0 and floats otherwise
  //   buffer_31 drives only 0 and floats otherwise
  //   buffer_32 drives only 0 and floats otherwise
  //   buffer_33 drives only 0 and floats otherwise
  //   buffer_34 drives only 0 and floats otherwise
  //   buffer_35 drives only 0 and floats otherwise
  //   buffer_36 drives only 0 and floats otherwise
  //   buffer_37 drives only 0 and floats otherwise
  //   buffer_38 drives only 0 and floats otherwise
  //   buffer_39 drives only 0 and floats otherwise
  //   buffer_40 drives only 0 and floats otherwise
  //   buffer_41 drives only 0 and floats otherwise
  //   buffer_42 drives only 0 and floats otherwise
  //   buffer_43 drives only 1 and floats otherwise
  //   buffer_44 drives only 1 and floats otherwise
  //   buffer_45 drives only 1 and floats otherwise
  //   buffer_46 drives only 1 and floats otherwise
  //   buffer_47 drives only 1 and floats otherwise
  //   buffer_48 drives only 1 and floats otherwise
  //   buffer_49 drives only 1 and floats otherwise
  //   buffer_50 drives only 1 and floats otherwise
  //   buffer_51 drives only 1 and floats otherwise
  //   buffer_52 drives only 1 and floats otherwise
  //   buffer_53 drives only 1 and floats otherwise
  //   buffer_54 drives only 1 and floats otherwise
  //   buffer_55 drives only 1 and floats otherwise
  //   buffer_56 drives only 1 and floats otherwise
  //   buffer_57 drives only 1 and floats otherwise
  //   buffer_58 drives only 1 and floats otherwise
  //   buffer_59 drives only 1 and floats otherwise
  //   buffer_60 drives only 1 and floats otherwise
  //   buffer_61 drives only 1 and floats otherwise
  //   buffer_62 drives only 1 and floats otherwise
  //   buffer_63 drives only 1 and floats otherwise
  //   buffer_64 drives only 1 and floats otherwise
  //   buffer_65 drives only 1 and floats otherwise
  //   buffer_66 drives only 1 and floats otherwise
  //   buffer_67 drives only 1 and floats otherwise
  //   buffer_68 drives only 1 and floats otherwise
  //   buffer_69 drives only 1 and floats otherwise
  //   buffer_70 drives only 1 and floats otherwise
  //   buffer_71 drives only 1 and floats otherwise
  //   buffer_72 drives only 1 and floats otherwise
  //   buffer_73 drives only 1 and floats otherwise
  //   buffer_74 drives only 1 and floats otherwise
  //   buffer_75 drives only 1 and floats otherwise
  //   buffer_76 drives only 1 and floats otherwise
  //   buffer_77 drives only 1 and floats otherwise
  //   buffer_78 drives only 1 and floats otherwise
  //   buffer_79 drives only 1 and floats otherwise
  //   buffer_80 drives only 1 and floats otherwise
  //   buffer_81 drives only 1 and floats otherwise
  //   buffer_82 drives only 1 and floats otherwise
  //   buffer_83 drives only 1 and floats otherwise
  //   buffer_84 drives only 1 and floats otherwise
  //   buffer_85 drives only 1 and floats otherwise
  //   buffer_86 drives only 1 and floats otherwise
  //   buffer_87 drives only 1 and floats otherwise
  //   buffer_88 drives only 1 and floats otherwise
  //   buffer_89 drives only 1 and floats otherwise
  //   buffer_90 drives only 1 and floats otherwise
  //   buffer_91 drives only 1 and floats otherwise
  //   buffer_92 drives only 1 and floats otherwise
  //   buffer_93 drives only 1 and floats otherwise
  //   buffer_94 drives only 1 and floats otherwise
  //   buffer_95 drives only 0 and floats otherwise
  //   buffer_96 drives only 0 and floats otherwise
  //    #0 i1 i3 i11
  //    #1 i3
  //    #2 i4 i5
  //    #3 i2 i4 
  //    #4 i1 i6
  //    #5 i9  
  //    #6 i5 i6
  //    #7 i2
  //    #8 i3 i11 i13 i14 
  //    #9 i3 i13 
  //   #10 i14 
  //   #11 i8 
  //   #12 i12 
  //   #13 i7 
  //   #14 i10 i12 
  //   #15 i10  
  //   i1  /0  /1      /3 
  //   i2   0   1      /3 
  //   i3      /1  /2 
  //   i4       1  /2  /3 
  //   i5  /0   1      /3 
  //   i6  /0       2  /3 
  //   i7   0  /1   2   3 
  //   i8   0   1  /2   3 
  //   i9   0  /1   2  /3 
  //   i10      1   2   3
  //   i11 /0  /1  /2 
  //   i12 /0       2   3 
  //   i13     /1  /2   3 
  //   i14 /0      /2   3 
  //          in3 in2 in1 in0    A B C D E F G
  //   i1      0   X   0   0     0 1 0 0 0 0 0   #0 #4
  //   i2      0   X   1   1     1 1 1 0 0 0 0   #3 #7
  //   i3      X   0   0   X     0 1 1 0 0 0 0   #0 #1 #8 #9 
  //   i4      0   0   1   X     0 1 0 1 0 0 1   #2 #3
  //   i5      0   X   1   0     1 0 0 1 1 0 0   #2 #6
  //   i6      0   1   X   0     0 0 1 0 0 1 1   #4 #6
  //   i7      1   1   0   1     0 1 1 1 1 0 1   #13
  //   i8      1   0   1   1     0 0 1 1 1 1 1   #11
  //   i9      0   1   0   1     1 0 1 1 0 1 1   #5 
  //   i10     1   1   1   X     1 0 0 0 1 1 1   #14 #15 
  //   i11     X   0   0   0     1 0 0 1 1 1 0   #0 #8 
  //   i12     1   1   X   0     1 0 0 1 1 1 0   #12 #14 
  //   i13     1   0   0   X     1 0 0 1 0 1 1   #8 #9 
  //   i14     1   0   X   0     1 1 1 0 1 1 1   #8 #10 
endmodule
